# Fritzing sketch arduino_uno_us (saved by Fritzing 1.0.1rc)
breadboards: 1

parts:
  HC-SR04_Sensor_1 = HC-SR04 Ultrasonic Distance Sensor
  LED1 = LED - 5mm [color="Red (633nm)" current=0.030A package="5 mm [THT]"]
  LED2 = LED - 5mm [color="Green (570nm)" current=0.030A package="5 mm [THT]"]
  R1 = Resistor [tolerance=±5% resistance=1k package="0402 [SMD]"]
  J1 = Piezo Speaker
  R2 = Resistor [tolerance=±5% power=0.5W resistance=1k package=THT]
  Part2 = Arduino Uno (Rev3) - ICSP
  R3 = Resistor [tolerance=±5% power=0.5W resistance=1k package=THT]

nets:
  VCC: HC-SR04_Sensor_1.VCC, Part2.3V3
  N1: HC-SR04_Sensor_1.TRIG, Part2.D2
  N2: HC-SR04_Sensor_1.ECHO, R3.Pin_1
  GND: HC-SR04_Sensor_1.GND, R1.Pin_0, J1.pin1, R2.Pin_0, Part2.GND
  N3: LED1.cathode, R2.Pin_1
  N4: LED1.anode, Part2.D10_PWM/SS
  N5: LED2.cathode, R1.Pin_1
  N6: LED2.anode, Part2.ICSP_MOSI, Part2.D11_PWM/MOSI
  N7: J1.pin2, Part2.D9_PWM
  N8: Part2.D4, R3.Pin_0
