# Fritzing sketch arduino_us (saved by Fritzing 1.0.1rc)
breadboards: 1

parts:
  Part1 = Arduino Mega 2560 (Rev3)
  HC-SR04_Sensor_1 = HC-SR04 Ultrasonic Distance Sensor
  LED1 = LED - 5mm [color="Red (633nm)" current=0.030A package="5 mm [THT]"]
  LED2 = LED - 5mm [color="Green (570nm)" current=0.030A package="5 mm [THT]"]
  R1 = Resistor [tolerance=±5% resistance=220 package="0402 [SMD]"]
  J1 = Piezo Speaker
  R2 = Resistor [tolerance=±5% resistance=220 package="0402 [SMD]"]

nets:
  N1: Part1.D16_PWM/TX2, HC-SR04_Sensor_1.TRIG
  N2: Part1.D15/RX3, HC-SR04_Sensor_1.ECHO
  N3: Part1.D13_PWM, J1.pin2
  N4: Part1.D12_PWM, LED2.anode
  N5: Part1.D11_PWM, LED1.anode
  5V: Part1.5V, HC-SR04_Sensor_1.VCC
  GND: Part1.GND, HC-SR04_Sensor_1.GND, R1.Pin_0, J1.pin1, R2.Pin_0
  N6: LED1.cathode, R2.Pin_1
  N7: LED2.cathode, R1.Pin_1
